# Fritzing sketch Sensor de GAS MQ-7 (saved by Fritzing 0.9.3b)

parts:
  U1 = GAS_SENSOR [package=mq-3]
  Componente1 = Arduino Mega 2560 (Rev3)

nets:
  N1: U1.A1, Componente1.A0
  N2: U1.H1, Componente1.GND
  N3: U1.H2, Componente1.5V
