# Fritzing sketch Ultrasonidos (saved by Fritzing 0.9.3b)
breadboards: 1

parts:
  Componente1 = Arduino Mega 2560 (Rev3)
  Ultrasónico_derecho = hc-sr04
  Ultrasonico_centro = hc-sr04
  Ultrasónico_izquierdo = hc-sr04

nets:
  GND: Componente1.GND, Ultrasónico_derecho.GND, Ultrasonico_centro.GND, Ultrasónico_izquierdo.GND
  VCC: Componente1.5V, Ultrasonico_centro.VCC, Ultrasónico_izquierdo.VCC
  N1: Componente1.D22, Ultrasonico_centro.Trig, Ultrasonico_centro.Echo
  N2: Componente1.D24, Ultrasónico_derecho.Trig, Ultrasónico_derecho.Echo
  N3: Componente1.D26, Ultrasónico_izquierdo.Trig, Ultrasónico_izquierdo.Echo
